// Logisim project Electron_CPU_16bit.circ as structural Verilog: 16 circuits, main circuit main
module main (
);

  wire clock_1_out, cpu_1_airi, cpu_1_airx, cpu_1_amar, cpu_1_apc, cpu_1_arf, cpu_1_atir, cpu_1_er, cpu_1_ew,
       cpu_1_hlt, cpu_1_kmar, cpu_1_kpc, cpu_1_ziri, DEBUG_out, toggle_1_o;
  wire [2:0] cpu_1_kalu, cpu_1_sel_1_in, cpu_1_sel_1_out, cpu_1_sel_2_in, cpu_1_sel_2_out, cpu_1_sel_3_in,
       cpu_1_sel_3_out, cpu_1_sel_add_in, cpu_1_sel_add_out;
  wire [4:0] cpu_1_beta;
  wire [9:0] cpu_1_ins;
  wire [15:0] cpu_1_a, cpu_1_b, cpu_1_bus_1, cpu_1_bus_2, cpu_1_bus_3, cpu_1_bus_add, cpu_1_r, cpu_1_ram;
  wire [63:0] W_R_sw1;

  Clock clock_1 (.out(clock_1_out));
  CPU cpu_1 (
    .CLK(clock_1_out), .DEBUG_mod(toggle_1_o), .DEBUG_signal(W_R_sw1), .Beta(cpu_1_beta), .A(cpu_1_a),
    .B(cpu_1_b), .BUS_3(cpu_1_bus_3), .BUS_Add(cpu_1_bus_add), .BUS_1(cpu_1_bus_1), .BUS_2(cpu_1_bus_2),
    .sel_1_in(cpu_1_sel_1_in), .sel_1_out(cpu_1_sel_1_out), .sel_2_in(cpu_1_sel_2_in),
    .sel_2_out(cpu_1_sel_2_out), .sel_3_in(cpu_1_sel_3_in), .sel_3_out(cpu_1_sel_3_out),
    .sel_Add_in(cpu_1_sel_add_in), .sel_Add_out(cpu_1_sel_add_out), .RAM(cpu_1_ram), .R(cpu_1_r),
    .eW(cpu_1_ew), .eR(cpu_1_er), .aMAR(cpu_1_amar), .kMAR(cpu_1_kmar), .kALU(cpu_1_kalu), .aRF(cpu_1_arf),
    .aIRx(cpu_1_airx), .aIRi(cpu_1_airi), .zIRi(cpu_1_ziri), .aTIR(cpu_1_atir), .aPC(cpu_1_apc),
    .kPC(cpu_1_kpc), .HLT(cpu_1_hlt), .INS(cpu_1_ins));  // open: IO_in, IO_out
  // Probe on cpu_1_beta
  DipSwitch #(.number(3)) Add_i (.sw1(W_R_sw1[35]), .sw2(W_R_sw1[34]), .sw3(W_R_sw1[33]));
  DipSwitch #(.number(3)) Add_o (.sw1(W_R_sw1[38]), .sw2(W_R_sw1[37]), .sw3(W_R_sw1[36]));
  // Probe on cpu_1_ew
  // Probe on cpu_1_sel_1_in
  // Probe on cpu_1_sel_1_out
  // Probe on cpu_1_ins
  DipSwitch #(.number(2)) W_R (.sw1(W_R_sw1[0]), .sw2(W_R_sw1[1]));
  DipSwitch #(.number(3)) In_1 (.sw1(W_R_sw1[17]), .sw2(W_R_sw1[16]), .sw3(W_R_sw1[15]));
  // Probe on cpu_1_amar
  // Probe on cpu_1_er
  // Probe on cpu_1_kmar
  // Probe on cpu_1_sel_2_in
  // Probe on cpu_1_bus_1
  // Probe on cpu_1_bus_2
  DipSwitch #(.number(2)) MAR (.sw1(W_R_sw1[2]), .sw2(W_R_sw1[3]));
  DipSwitch #(.number(3)) ALU (.sw1(W_R_sw1[6]), .sw2(W_R_sw1[5]), .sw3(W_R_sw1[4]));
  DipSwitch #(.number(3)) Out_1 (.sw1(W_R_sw1[20]), .sw2(W_R_sw1[19]), .sw3(W_R_sw1[18]));
  DipSwitch #(.number(3)) In_2 (.sw1(W_R_sw1[23]), .sw2(W_R_sw1[22]), .sw3(W_R_sw1[21]));
  // Probe on cpu_1_kalu
  // Probe on cpu_1_arf
  // Probe on cpu_1_sel_2_out
  // Probe on cpu_1_bus_add
  // Probe on cpu_1_bus_3
  DipSwitch #(.number(2)) RF_IRx (.sw1(W_R_sw1[7]), .sw2(W_R_sw1[8]));
  DipSwitch #(.number(2)) IRi (.sw1(W_R_sw1[9]), .sw2(W_R_sw1[10]));
  DipSwitch #(.number(3)) Out_2 (.sw1(W_R_sw1[26]), .sw2(W_R_sw1[25]), .sw3(W_R_sw1[24]));
  // Probe on cpu_1_airx
  // Probe on cpu_1_airi
  // Probe on cpu_1_ziri
  // Probe on cpu_1_sel_3_in
  // Probe on cpu_1_sel_3_out
  // Probe on cpu_1_a
  // Probe on cpu_1_ram
  DipSwitch #(.number(4)) TIR_PC_HLT (.sw1(W_R_sw1[11]), .sw2(W_R_sw1[12]), .sw3(W_R_sw1[13]), .sw4(W_R_sw1[14]));
  DipSwitch #(.number(3)) In_3 (.sw1(W_R_sw1[29]), .sw2(W_R_sw1[28]), .sw3(W_R_sw1[27]));
  DipSwitch #(.number(3)) Out_3 (.sw1(W_R_sw1[32]), .sw2(W_R_sw1[31]), .sw3(W_R_sw1[30]));
  // Probe on cpu_1_atir
  // Probe on cpu_1_apc
  // Probe on cpu_1_sel_add_in
  // Probe on cpu_1_b
  // Probe on cpu_1_r
  // Probe on W_R_sw1
  Toggle toggle_1 (.I(DEBUG_out), .O(toggle_1_o));
  Button DEBUG (.out(DEBUG_out));
  // Probe on cpu_1_hlt
  // Probe on cpu_1_kpc
  // Probe on cpu_1_sel_add_out
endmodule

module CPU (
  input  DEBUG_mod,
  input  [63:0] DEBUG_signal,
  input  [15:0] IO_in,
  input  CLK,
  output [15:0] IO_out,
  output [15:0] BUS_1,
  output [4:0] Beta,
  output eW,
  output [9:0] INS,
  output eR,
  output aMAR,
  output kMAR,
  output [2:0] kALU,
  output [2:0] sel_1_in,
  output aRF,
  output [2:0] sel_1_out,
  output aIRx,
  output [2:0] sel_2_in,
  output aIRi,
  output zIRi,
  output [2:0] sel_2_out,
  output [15:0] BUS_2,
  output aTIR,
  output [2:0] sel_3_in,
  output aPC,
  output [2:0] sel_3_out,
  output kPC,
  output HLT,
  output [2:0] sel_Add_in,
  output [2:0] sel_Add_out,
  output [15:0] RAM,
  output [15:0] R,
  output [15:0] A,
  output [15:0] BUS_3,
  output [15:0] B,
  output [15:0] BUS_Add
);

  wire and_1_out, and_2_out, or_1_out, ou_1_clk_h;
  wire [15:0] ADD_DATA, DATA_ADD, IRx_in, IRx_out, MAR_in, MAR_out, PC_in, PC_out, RAM_in, RF_in_i, RF_out_i,
       RF_out_j, TIR_in;

  and and_1 (and_1_out, ~sel_1_in[0], sel_1_in[1], ~sel_1_in[2]);  // AND_Gate
  or or_1 (or_1_out, and_1_out, and_2_out);
  and and_2 (and_2_out, ~sel_3_in[0], sel_3_in[1], ~sel_3_in[2]);  // AND_Gate
  CU cu_1 (
    .INS(INS), .beta(Beta), .CLK(ou_1_clk_h), .DEBUG(DEBUG_signal), .DEBUG_mod(DEBUG_mod), .eW(eW), .eR(eR),
    .aMAR(aMAR), .kMAR(kMAR), .kALU(kALU), .aRF(aRF), .aIRx(aIRx), .aIRi(aIRi), .zIRi(zIRi), .aTIR(aTIR),
    .aPC(aPC), .kPC(kPC), .HLT(HLT), .DATA_1_in(sel_1_in), .DATA_1_out(sel_1_out), .DATA_2_in(sel_2_in),
    .DATA_2_out(sel_2_out), .DATA_3_in(sel_3_in), .DATA_3_out(sel_3_out), .ADD_in(sel_Add_in),
    .ADD_out(sel_Add_out));
  OU ou_1 (
    .eW(eW), .eR(eR), .aRF(aRF), .RF_in_i(RF_in_i), .MAR_in(MAR_in), .aMAR(aMAR), .kMAR(kMAR),
    .RAM_in(RAM_in), .HLT(HLT), .CLK(CLK), .PC_in(PC_in), .kALU(kALU), .A(A), .B(B), .aPC(aPC), .kPC(kPC),
    .aTIR(aTIR), .R_sel(or_1_out), .TIR_in(TIR_in), .IRx_in(IRx_in), .zIRi(zIRi), .aIRi(aIRi), .aIRx(aIRx),
    .IRx_out(IRx_out), .RF_out_j(RF_out_j), .RF_out_i(RF_out_i), .RAM_out(RAM), .MAR_out(MAR_out),
    .CLK_h(ou_1_clk_h), .R(R), .PC_out(PC_out), .beta(Beta), .INS(INS));
  DATA_BUS DATA_BUS_1 (
    .IN_3(IRx_out), .IN_0(ADD_DATA), .IN_1(RAM), .IN_2(R), .In_sel(sel_1_in), .Out_sel(sel_1_out),
    .Info(BUS_1), .OUT_0(DATA_ADD), .OUT_1(RAM_in), .OUT_2(RF_in_i), .OUT_3(IRx_in), .OUT_4(TIR_in),
    .OUT_5(IO_out));  // open: IN_4, IN_5, IN_6, IN_7, OUT_6, OUT_7
  DATA_BUS DATA_BUS_2 (
    .IN_3(IRx_out), .IN_0(ADD_DATA), .IN_1(RAM), .IN_2(RF_out_j), .In_sel(sel_2_in), .Out_sel(sel_2_out),
    .Info(BUS_2), .OUT_0(DATA_ADD), .OUT_1(RAM_in), .OUT_2(A), .OUT_3(IRx_in), .OUT_4(TIR_in));  // open: IN_4, IN_5, IN_6, IN_7, OUT_5, OUT_6, OUT_7
  DATA_BUS DATA_BUS_3 (
    .IN_3(RF_out_i), .IN_4(IRx_out), .IN_5(IO_in), .IN_0(ADD_DATA), .IN_1(RAM), .IN_2(R), .In_sel(sel_3_in),
    .Out_sel(sel_3_out), .Info(BUS_3), .OUT_0(DATA_ADD), .OUT_1(RAM_in), .OUT_2(B), .OUT_3(IRx_in),
    .OUT_4(TIR_in));  // open: IN_6, IN_7, OUT_5, OUT_6, OUT_7
  DATA_BUS ADD_BUS (
    .IN_3(IRx_out), .IN_4(PC_out), .IN_1(DATA_ADD), .IN_2(MAR_out), .In_sel(sel_Add_in),
    .Out_sel(sel_Add_out), .Info(BUS_Add), .OUT_1(ADD_DATA), .OUT_2(MAR_in), .OUT_3(PC_in));  // open: IN_5, IN_6, IN_7, IN_0, OUT_0, OUT_4, OUT_5, OUT_6, OUT_7

  // Other names for the same wires on the sheet: BUS_1_in[2:0] = sel_1_in; BUS_1_out[2:0] = sel_1_out;
  //   BUS_2_in[2:0] = sel_2_in; BUS_2_out[2:0] = sel_2_out; BUS_3_in[2:0] = sel_3_in; BUS_3_out[2:0] = sel_3_out;
  //   BUS_Add_in[2:0] = sel_Add_in; BUS_Add_out[2:0] = sel_Add_out; RAM_out[15:0] = RAM
endmodule

module CU (
  input  [9:0] INS,
  input  [4:0] beta,
  input  CLK,
  input  DEBUG_mod,
  input  [63:0] DEBUG,
  output eW,
  output eR,
  output aMAR,
  output kMAR,
  output [2:0] kALU,
  output aRF,
  output aIRx,
  output aIRi,
  output zIRi,
  output aTIR,
  output aPC,
  output kPC,
  output HLT,
  output [2:0] DATA_1_in,
  output [2:0] DATA_1_out,
  output [2:0] DATA_2_in,
  output [2:0] DATA_2_out,
  output [2:0] DATA_3_in,
  output [2:0] DATA_3_out,
  output [2:0] ADD_in,
  output [2:0] ADD_out
);

  wire [4:0] uINS_q, y;
  wire [63:0] rom_1_data;
  wire [63:39] multiplexer_1_out;

  Register #(.width(5)) uINS (.D(y), .en(1'b1), .clk(CLK), .Q(uINS_q));  // open: clr
  // Probe on y
  ROM #(.addrWidth(24), .dataWidth(64)) rom_1 (.addr({uINS_q, 4'b0000, beta, INS}), .data(rom_1_data));
  Multiplexer #(.width(64)) multiplexer_1 (
    .in0(rom_1_data), .in1(DEBUG),
    .out({multiplexer_1_out[63], y, multiplexer_1_out[57:39], ADD_out, ADD_in, DATA_3_out, DATA_3_in, DATA_2_out, DATA_2_in, DATA_1_out, DATA_1_in, HLT, kPC, aPC, aTIR, zIRi, aIRi, aIRx, aRF, kALU, kMAR, aMAR, eR, eW}),
    .sel(DEBUG_mod));

  // Notes on the sheet:
  //   contents of rom_1 (hex, n*v repeats v):
  //   400002800000004 0 0 0 40000009a490080 0 0 0 40000009a490090 0 0 0 40000009a4900d0 0 0 0
  //   40000009a4900e0 0 0 0 40000009a4900f0 0 0 4000000980900a0 0 0 4000000980900b0 0 0 4000000980900c0 0
  //   0 0 400001200480080 64*0 4000 400000000000000 413*0 400002600000004 40000009a690080 4000022a2410004
  //   0 400002600000004 40000009a690090 4000022a2410004 0 400002600000004 40000009a6900d0 4000022a2410004
  //   0 400002600000004 40000009a6900e0 4000022a2410004 0 400002600000004 40000009a6900f0 4000022a2410004
  //   0 400002600000004 400002600000004 0 400002600000004 400002600000004 0 400002600000004
  //   400002600000004 0 400002600000004 400000000098080 4000022a2410004 0 400002600000004 4000022a2410004
  //   400003600001000 8*800000000000000 467*0 400002800000004 0 0 0 40000009a490080 0 0 0 40000009a490090
  //   0 0 0 40000009a4900d0 0 0 0 40000009a4900e0 0 0 0 40000009a4900f0 0 0 4000000980900a0 0 0
  //   4000000980900b0 0 0 4000000980900c0 0 0 0 400001200480080 64*0 4000 400000000000000 413*0
  //   400002600000004 40000009a690080 4000022a2410004 0 400002600000004 40000009a690090 4000022a2410004 0
  //   400002600000004 40000009a6900d0 4000022a2410004 0 400002600000004 40000009a6900e0 4000022a2410004 0
  //   400002600000004 40000009a6900f0 4000022a2410004 0 400002600000004 400002600000004 0 400002600000004
  //   400002600000004 0 400002600000004 400002600000004 0 400002600000004 400000000098080 4000022a2410004
  //   0 400002600000004 4000022a2410004 400003600001000 400000000000000 400000000000000 6*800000000000000
  //   467*0 400002800000004 0 0 0 40000009a490080 0 0 0 40000009a490090 0 0 0 40000009a4900d0 0 0 0
  //   40000009a4900e0 0 0 0 40000009a4900f0 0 0 4000000980900a0 0 0 4000000980900b0 0 0 4000000980900c0 0
  //   0 0 400001200480080 64*0 4000 400000000000000 413*0 400002600000004 40000009a690080 4000022a2410004
  //   0 400002600000004 40000009a690090 4000022a2410004 0 400002600000004 40000009a6900d0 4000022a2410004
  //   0 400002600000004 40000009a6900e0 4000022a2410004 0 400002600000004 40000009a6900f0 4000022a2410004
  //   0 400002600000004 400002600000004 0 400002600000004 400002600000004 0 400002600000004
  //   400002600000004 0 400002600000004 400000000098080 4000022a2410004 0 400002600000004 4000022a2410004
  //   400003600001000 800000000000000 800000000000000 400000000000000 400000000000000 4*800000000000000
  //   467*0 400002800000004 0 0 0 40000009a490080 0 0 0 40000009a490090 0 0 0 40000009a4900d0 0 0 0
  //   40000009a4900e0 0 0 0 40000009a4900f0 0 0 4000000980900a0 0 0 4000000980900b0 0 0 4000000980900c0 0
  //   0 0 400001200480080 64*0 4000 400000000000000 413*0 400002600000004 40000009a690080 4000022a2410004
  //   0 400002600000004 40000009a690090 4000022a2410004 0 400002600000004 40000009a6900d0 4000022a2410004
  //   0 400002600000004 40000009a6900e0 4000022a2410004 0 400002600000004 40000009a6900f0 4000022a2410004
  //   0 400002600000004 400002600000004 0 400002600000004 400002600000004 0 400002600000004
  //   400002600000004 0 400002600000004 400000000098080 4000022a2410004 0 400002600000004 4000022a2410004
  //   400003600001000 4*400000000000000 4*800000000000000 467*0 400002800000004 0 0 0 40000009a490080 0 0
  //   0 40000009a490090 0 0 0 40000009a4900d0 0 0 0 40000009a4900e0 0 0 0 40000009a4900f0 0 0
  //   4000000980900a0 0 0 4000000980900b0 0 0 4000000980900c0 0 0 0 400001200480080 64*0 4000
  //   400000000000000 413*0 400002600000004 40000009a690080 4000022a2410004 0 400002600000004
  //   40000009a690090 4000022a2410004 0 400002600000004 40000009a6900d0 4000022a2410004 0 400002600000004
  //   40000009a6900e0 4000022a2410004 0 400002600000004 40000009a6900f0 4000022a2410004 0 400002600000004
  //   400002600000004 0 400002600000004 400002600000004 0 400002600000004 400002600000004 0
  //   400002600000004 400000000098080 4000022a2410004 0 400002600000004 4000022a2410004 400003600001000
  //   4*800000000000000 400000000000000 400000000000000 800000000000000 800000000000000 467*0
  //   400002800000004 0 0 0 40000009a490080 0 0 0 40000009a490090 0 0 0 40000009a4900d0 0 0 0
  //   40000009a4900e0 0 0 0 40000009a4900f0 0 0 4000000980900a0 0 0 4000000980900b0 0 0 4000000980900c0 0
  //   0 0 400001200480080 64*0 4000 400000000000000 413*0 400002600000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
endmodule

module OU (
  input  [15:0] PC_in,
  input  [15:0] RAM_in,
  input  [15:0] B,
  input  [15:0] MAR_in,
  input  [15:0] A,
  input  [15:0] TIR_in,
  input  [15:0] IRx_in,
  input  [15:0] RF_in_i,
  input  CLK,
  input  HLT,
  input  R_sel,
  input  eW,
  input  [2:0] kALU,
  input  aTIR,
  input  zIRi,
  input  aRF,
  input  eR,
  input  aIRi,
  input  aPC,
  input  aMAR,
  input  kPC,
  input  aIRx,
  input  kMAR,
  output [15:0] RF_out_j,
  output [15:0] PC_out,
  output [15:0] MAR_out,
  output [15:0] IRx_out,
  output [15:0] RF_out_i,
  output [15:0] RAM_out,
  output [15:0] R,
  output CLK_h,
  output [4:0] beta,
  output [9:0] INS
);

  wire [2:0] ir_1_i, ir_1_j;
  wire [3:0] alu_1_flags;
  wire [15:0] tir_1_tir_out;

  Memory memory_1 (
    .kMAR(kMAR), .MAR_in(MAR_in), .aMAR(aMAR), .CLK(CLK_h), .eW(eW), .eR(eR), .RAM_in(RAM_in),
    .MAR_out(MAR_out), .RAM_out(RAM_out));
  CLK_HLT clk_hlt_1 (.HLT(HLT), .CLK_in(CLK), .CLK_out(CLK_h));
  PC pc_1 (.kPC(kPC), .aPC(aPC), .CLK(CLK_h), .PC_in(PC_in), .PC_out(PC_out));
  ALU alu_1 (.kALU(kALU), .A(A), .B(B), .R(R), .Flags(alu_1_flags));
  Register #(.width(4)) Flags (.D(alu_1_flags), .en(R_sel), .clk(CLK_h), .Q(beta[3:0]));  // open: clr
  TIR tir_1 (.aTIR(aTIR), .TIR_in(TIR_in), .CLK(CLK_h), .TIR_out(tir_1_tir_out), .b5(beta[4]));
  IR ir_1 (
    .aIRx(aIRx), .CLK(CLK_h), .IRi_in(tir_1_tir_out), .IRx_in(IRx_in), .zIRi(zIRi), .aIRi(aIRi),
    .IRx_out(IRx_out), .i(ir_1_i), .j(ir_1_j), .INS(INS));
  RF rf_1 (.INi(RF_in_i), .aRF(aRF), .i(ir_1_i), .j(ir_1_j), .CLK(CLK_h), .OUTi(RF_out_i), .OUTj(RF_out_j));
endmodule

module Memory (
  input  [15:0] MAR_in,
  input  kMAR,
  input  aMAR,
  input  eW,
  input  eR,
  input  CLK,
  input  [15:0] RAM_in,
  output [15:0] MAR_out,
  output [15:0] RAM_out
);

  wire not_1_out;
  wire [15:0] adder_1_out, multiplexer_1_out;

  Adder #(.width(16)) adder_1 (.a(MAR_out), .b(16'h1), .out(adder_1_out));  // open: cin, cout
  Register #(.width(16)) MAR (.D(multiplexer_1_out), .en(aMAR), .clk(CLK), .Q(MAR_out));  // open: clr
  Multiplexer #(.width(16)) multiplexer_1 (.in0(adder_1_out), .in1(MAR_in), .out(multiplexer_1_out), .sel(not_1_out));
  not not_1 (not_1_out, kMAR);
  RAM #(.addrWidth(16), .asyncread("true"), .dataWidth(16), .trigger("falling")) ram_1 (
    .addr(MAR_out), .we(eW), .oe(eR), .clk(CLK), .din(RAM_in), .dout(RAM_out));
endmodule

module ALU (
  input  [15:0] A,
  input  [15:0] B,
  input  [2:0] kALU,
  output [15:0] R,
  output [3:0] Flags
);

  wire alu_controller_1_invb, alu_controller_1_rplus;
  wire [1:0] alu_controller_1_rmux;
  wire [15:0] adder_1_out, alu_controller_1_za, and_1_out, and_2_out, multiplexer_1_out, not_1_out, or_1_out,
       xor_1_out;

  assign and_1_out = A & alu_controller_1_za;  // AND_Gate and_1, 16 bits wide
  assign not_1_out = ~B;  // NOT_Gate not_1, 16 bits wide
  Multiplexer #(.width(16)) multiplexer_1 (
    .in0(B), .in1(not_1_out), .out(multiplexer_1_out), .sel(alu_controller_1_invb));
  ALU_controller alu_controller_1 (
    .kALU(kALU), .rPlus(alu_controller_1_rplus), .invB(alu_controller_1_invb), .rMUX(alu_controller_1_rmux),
    .zA(alu_controller_1_za));
  Adder #(.width(16)) adder_1 (
    .a(and_1_out), .b(multiplexer_1_out), .out(adder_1_out), .cin(alu_controller_1_rplus), .cout(Flags[2]));
  assign and_2_out = and_1_out & multiplexer_1_out;  // AND_Gate and_2, 16 bits wide
  assign or_1_out = and_1_out | multiplexer_1_out;  // OR_Gate or_1, 16 bits wide
  assign xor_1_out = and_1_out ^ multiplexer_1_out;  // XOR_Gate xor_1, 16 bits wide
  Multiplexer #(.select(2), .width(16)) multiplexer_2 (
    .in0(adder_1_out), .in1(and_2_out), .in2(or_1_out), .in3(xor_1_out), .out({Flags[1], R[14:0]}),
    .sel(alu_controller_1_rmux));
  Overflow overflow_1 (.A(and_1_out), .B(multiplexer_1_out), .R({Flags[1], R[14:0]}), .out_4(Flags[0]));
  OR_bitwise or_bitwise_1 (.R({Flags[1], R[14:0]}), .zF(Flags[3]));

  assign R[15] = Flags[1];
endmodule

module ALU_controller (
  input  [2:0] kALU,
  output [15:0] zA,
  output rPlus,
  output invB,
  output [1:0] rMUX
);

  wire and_1_out;

  and and_1 (and_1_out, ~kALU[1], ~kALU[2]);  // AND_Gate
  or or_1 (rPlus, kALU[0], kALU[1]);
  or or_2 (invB, kALU[0], kALU[2]);
  and and_2 (rMUX[1], kALU[1], kALU[2]);
  and and_3 (rMUX[0], kALU[0], kALU[2]);
  assign zA = {{15{and_1_out}}, and_1_out};  // Bit_Extender bit_extender_1
endmodule

module OR_bitwise (
  input  [15:0] R,
  output zF
);

  nor nor_1 (zF, R[0], R[1], R[2], R[3], R[4], R[5], R[6], R[7], R[8], R[9], R[10], R[11], R[12], R[13], R[14], R[15]);
endmodule

module Overflow (
  input  [15:0] A,
  input  [15:0] B,
  input  [15:0] R,
  output out_4
);

  wire and_1_out, and_2_out;

  and and_1 (and_1_out, ~A[15], ~B[15], R[15]);  // AND_Gate
  and and_2 (and_2_out, A[15], B[15], ~R[15]);  // AND_Gate
  or or_1 (out_4, and_1_out, and_2_out);
endmodule

module RF (
  input  [15:0] INi,
  input  aRF,
  input  [2:0] i,
  input  [2:0] j,
  input  CLK,
  output [15:0] OUTi,
  output [15:0] OUTj
);

  wire demultiplexer_1_out0, demultiplexer_1_out1, demultiplexer_1_out2, demultiplexer_1_out3,
       demultiplexer_1_out4, demultiplexer_1_out5, demultiplexer_1_out6, demultiplexer_1_out7;
  wire [15:0] RF_0_q, RF_1_q, RF_2_q, RF_3_q, RF_4_q, RF_5_q, RF_6_q, RF_7_q;

  Demultiplexer #(.select(3)) demultiplexer_1 (
    .out0(demultiplexer_1_out0), .out1(demultiplexer_1_out1), .out2(demultiplexer_1_out2),
    .out3(demultiplexer_1_out3), .out4(demultiplexer_1_out4), .out5(demultiplexer_1_out5),
    .out6(demultiplexer_1_out6), .out7(demultiplexer_1_out7), .in(aRF), .sel(i));
  Register #(.width(16)) RF_0 (.D(INi), .en(demultiplexer_1_out0), .clk(CLK), .Q(RF_0_q));  // open: clr
  Register #(.width(16)) RF_2 (.D(INi), .en(demultiplexer_1_out2), .clk(CLK), .Q(RF_2_q));  // open: clr
  Register #(.width(16)) RF_4 (.D(INi), .en(demultiplexer_1_out4), .clk(CLK), .Q(RF_4_q));  // open: clr
  Register #(.width(16)) RF_6 (.D(INi), .en(demultiplexer_1_out6), .clk(CLK), .Q(RF_6_q));  // open: clr
  Register #(.width(16)) RF_1 (.D(INi), .en(demultiplexer_1_out1), .clk(CLK), .Q(RF_1_q));  // open: clr
  Register #(.width(16)) RF_3 (.D(INi), .en(demultiplexer_1_out3), .clk(CLK), .Q(RF_3_q));  // open: clr
  Register #(.width(16)) RF_5 (.D(INi), .en(demultiplexer_1_out5), .clk(CLK), .Q(RF_5_q));  // open: clr
  Register #(.width(16)) RF_7 (.D(INi), .en(demultiplexer_1_out7), .clk(CLK), .Q(RF_7_q));  // open: clr
  Multiplexer #(.select(3), .width(16)) multiplexer_1 (
    .in0(RF_0_q), .in1(RF_1_q), .in2(RF_2_q), .in3(RF_3_q), .in4(RF_4_q), .in5(RF_5_q), .in6(RF_6_q),
    .in7(RF_7_q), .out(OUTi), .sel(i));
  Multiplexer #(.select(3), .width(16)) multiplexer_2 (
    .in0(RF_0_q), .in1(RF_1_q), .in2(RF_2_q), .in3(RF_3_q), .in4(RF_4_q), .in5(RF_5_q), .in6(RF_6_q),
    .in7(RF_7_q), .out(OUTj), .sel(j));
endmodule

module IR (
  input  [15:0] IRx_in,
  input  aIRx,
  input  CLK,
  input  aIRi,
  input  [15:0] IRi_in,
  input  zIRi,
  output [15:0] IRx_out,
  output [2:0] i,
  output [2:0] j,
  output [9:0] INS
);

  wire [15:0] multiplexer_1_out;

  Register #(.width(16)) IRx (.D(IRx_in), .en(aIRx), .clk(CLK), .Q(IRx_out));  // open: clr
  Register #(.width(16)) IRi (.D(multiplexer_1_out), .en(aIRi), .clk(CLK), .Q({INS, j, i}));  // open: clr
  Multiplexer #(.width(16)) multiplexer_1 (.in0(IRi_in), .in1({16{1'b0}}), .out(multiplexer_1_out), .sel(zIRi));
endmodule

module TIR (
  input  [15:0] TIR_in,
  input  aTIR,
  input  CLK,
  output [15:0] TIR_out,
  output b5
);

  wire not_1_out;

  Register #(.width(16)) register_1 (.D(TIR_in), .en(aTIR), .clk(not_1_out), .Q({b5, TIR_out[14:0]}));  // open: clr
  not not_1 (not_1_out, CLK);

  assign TIR_out[15] = b5;
endmodule

module PC (
  input  [15:0] PC_in,
  input  kPC,
  input  aPC,
  input  CLK,
  output [15:0] PC_out
);

  wire [15:0] adder_1_out, multiplexer_1_out;

  Adder #(.width(16)) adder_1 (.a(16'h1), .b(PC_out), .out(adder_1_out));  // open: cin, cout
  Register #(.width(16)) register_1 (.D(multiplexer_1_out), .en(aPC), .clk(CLK), .Q(PC_out));  // open: clr
  Multiplexer #(.width(16)) multiplexer_1 (.in0(PC_in), .in1(adder_1_out), .out(multiplexer_1_out), .sel(kPC));
endmodule

module DATA_BUS (
  input  [15:0] IN_0,
  input  [15:0] IN_1,
  input  [15:0] IN_2,
  input  [15:0] IN_3,
  input  [15:0] IN_4,
  input  [15:0] IN_5,
  input  [15:0] IN_6,
  input  [15:0] IN_7,
  input  [2:0] In_sel,
  input  [2:0] Out_sel,
  output [15:0] Info,
  output [15:0] OUT_0,
  output [15:0] OUT_1,
  output [15:0] OUT_2,
  output [15:0] OUT_3,
  output [15:0] OUT_4,
  output [15:0] OUT_5,
  output [15:0] OUT_6,
  output [15:0] OUT_7
);

  wire decoder_1_out0, decoder_1_out1, decoder_1_out2, decoder_1_out3, decoder_1_out4, decoder_1_out5,
       decoder_1_out6, decoder_1_out7;

  Multiplexer #(.select(3), .width(16)) multiplexer_1 (
    .in0(IN_0), .in1(IN_1), .in2(IN_2), .in3(IN_3), .in4(IN_4), .in5(IN_5), .in6(IN_6), .in7(IN_7),
    .out(Info), .sel(In_sel));
  assign OUT_0 = decoder_1_out0 ? Info : 16'bz;  // Controlled_Buffer controlled_buffer_1
  assign OUT_1 = decoder_1_out1 ? Info : 16'bz;  // Controlled_Buffer controlled_buffer_2
  assign OUT_2 = decoder_1_out2 ? Info : 16'bz;  // Controlled_Buffer controlled_buffer_3
  assign OUT_3 = decoder_1_out3 ? Info : 16'bz;  // Controlled_Buffer controlled_buffer_4
  assign OUT_4 = decoder_1_out4 ? Info : 16'bz;  // Controlled_Buffer controlled_buffer_5
  assign OUT_5 = decoder_1_out5 ? Info : 16'bz;  // Controlled_Buffer controlled_buffer_6
  assign OUT_6 = decoder_1_out6 ? Info : 16'bz;  // Controlled_Buffer controlled_buffer_7
  assign OUT_7 = decoder_1_out7 ? Info : 16'bz;  // Controlled_Buffer controlled_buffer_8
  Decoder #(.select(3)) decoder_1 (
    .out0(decoder_1_out0), .out1(decoder_1_out1), .out2(decoder_1_out2), .out3(decoder_1_out3),
    .out4(decoder_1_out4), .out5(decoder_1_out5), .out6(decoder_1_out6), .out7(decoder_1_out7), .sel(Out_sel));  // open: en
endmodule

module CLK_HLT (
  input  CLK_in,
  input  HLT,
  output CLK_out
);

  and and_1 (CLK_out, CLK_in, ~HLT);  // AND_Gate
endmodule

module Toggle (
  input  I,
  output O
);

  T_Flip_Flop t_ff_1 (.T(1'b1), .clk(I), .Q(O));  // open: Qn, reset, preset
endmodule
